// Logisim project single cycle cpu3.circ as structural Verilog: 14 circuits, main circuit SingleCycleCPU
module SingleCycleCPU (
);

  wire alucontrol_1_sub, clock_1_out, clock_2_out, control_unit_1_alusrc, control_unit_1_beq,
       control_unit_1_bne, control_unit_1_jump, control_unit_1_memread, control_unit_1_memtoreg,
       control_unit_1_memwrite, control_unit_1_r_type, control_unit_1_regdest, control_unit_1_regwrite,
       ExtOp, pull_resistor_1_node, Zero;
  wire [1:0] pccontroller_1_pc;
  wire [2:0] alucontrol_1_alucntrl;
  wire [3:0] control_unit_1_aluop, register_1_q_2;
  wire [4:0] multiplexer_2_out;
  wire [5:0] Funct, Opcode;
  wire [25:0] register_1_q;
  wire [25:6] ram_1_data;
  wire [29:0] adder_1_out, adder_2_out, multiplexer_1_out;
  wire [31:0] ALU_out_5, Extender_out, multiplexer_3_out, multiplexer_4_out, ram_2_data,
       register_file_1_bus_a, register_file_1_bus_b, shifter_1_out;

  // Probe on multiplexer_1_out
  PCController pccontroller_1 (
    .PC(pccontroller_1_pc), .Zero(Zero), .Jump(control_unit_1_jump), .BNE(control_unit_1_bne),
    .BEQ(control_unit_1_beq));
  Register #(.width(30), .trigger("falling")) register_1 (
    .D(multiplexer_1_out), .Q({register_1_q_2, register_1_q}), .clk(clock_1_out));  // open: en, clr
  Multiplexer #(.select(2), .width(30)) multiplexer_1 (
    .in0(adder_1_out), .in1(adder_2_out), .in2({register_1_q_2, ram_1_data, Funct}), .out(multiplexer_1_out),
    .sel(pccontroller_1_pc));  // open: in3, en
  Clock clock_1 (.out(clock_1_out));
  Adder #(.width(30)) adder_1 (.a({register_1_q_2, register_1_q}), .b(30'h1), .out(adder_1_out));  // open: cin, cout
  Pull_Resistor #(.pull(1)) pull_resistor_1 (.node(pull_resistor_1_node));
  RAM #(.addrWidth(24), .dataWidth(32)) ram_1 (
    .addr(register_1_q[23:0]), .data({Opcode, ram_1_data, Funct}), .ld(pull_resistor_1_node));  // open: sel, clk, clr
  Control_Unit control_unit_1 (
    .Opcode(Opcode), .RegDest(control_unit_1_regdest), .BNE(control_unit_1_bne), .BEQ(control_unit_1_beq),
    .MemWrite(control_unit_1_memwrite), .MemRead(control_unit_1_memread), .MemToReg(control_unit_1_memtoreg),
    .RegWrite(control_unit_1_regwrite), .ALUSrc(control_unit_1_alusrc), .ExtOp(ExtOp),
    .Jump(control_unit_1_jump), .ALUOp(control_unit_1_aluop), .R_Type(control_unit_1_r_type));
  // Probe on ram_1_data[25:21]
  // Probe on ram_1_data[20:16]
  Multiplexer #(.width(5)) multiplexer_2 (
    .in0(ram_1_data[20:16]), .in1(ram_1_data[15:11]), .out(multiplexer_2_out), .sel(control_unit_1_regdest));  // open: en
  // Probe on multiplexer_2_out
  Extender Extender (.Imm({ram_1_data[15:6], Funct}), .Out(Extender_out), .ExtOp(ExtOp));
  Register_File register_file_1 (
    .RA(ram_1_data[25:21]), .RB(ram_1_data[20:16]), .RW(multiplexer_2_out), .Bus_A(register_file_1_bus_a),
    .Bus_B(register_file_1_bus_b), .RegWrite(control_unit_1_regwrite), .Bus_W(multiplexer_4_out));
  // Probe on multiplexer_4_out
  Shifter #(.width(32)) shifter_1 (.in(Extender_out), .\dist (5'b00010), .out(shifter_1_out));
  Adder #(.width(30)) adder_2 (.a(adder_1_out), .b(shifter_1_out[31:2]), .out(adder_2_out));  // open: cin, cout
  // Probe on register_file_1_bus_a
  // Probe on multiplexer_3_out
  Multiplexer #(.width(32)) multiplexer_3 (
    .in0(register_file_1_bus_b), .in1(Extender_out), .out(multiplexer_3_out), .sel(control_unit_1_alusrc));  // open: en
  ALUControl alucontrol_1 (
    .MainCntrl(control_unit_1_aluop), .Funct(Funct), .in_3(control_unit_1_r_type), .Sub(alucontrol_1_sub),
    .ALUCntrl(alucontrol_1_alucntrl));
  _32_Bit_ALU ALU (
    .Bus_A(register_file_1_bus_a), .Bus_B(multiplexer_3_out), .out_5(ALU_out_5), .Zero_flag(Zero),
    .Sub(alucontrol_1_sub), .Op(alucontrol_1_alucntrl));
  Multiplexer #(.width(32)) multiplexer_4 (
    .in0(ALU_out_5), .in1(ram_2_data), .out(multiplexer_4_out), .sel(control_unit_1_memtoreg));  // open: en
  // Probe on Funct
  // Probe on register_file_1_bus_b
  Clock clock_2 (.out(clock_2_out));
  RAM #(.addrWidth(24), .dataWidth(32), .bus("separate")) ram_2 (
    .addr(ALU_out_5[25:2]), .din(register_file_1_bus_b), .data(ram_2_data), .str(control_unit_1_memwrite),
    .clk(clock_2_out), .ld(control_unit_1_memread));  // open: sel, clr
endmodule

module _1_bit_ALU (
  input  Sub,
  input  Cin,
  input  [2:0] in_3,
  input  A,
  input  B,
  input  Less,
  output Result,
  output C_out,
  output out_9
);

  wire and_1_out, nor_1_out, or_1_out, xor_1_out, xor_2_out;

  Adder #(.width(1)) adder_1 (.a(A), .b(xor_1_out), .out(out_9), .cin(Cin), .cout(C_out));
  xor xor_1 (xor_1_out, B, Sub);
  and and_1 (and_1_out, A, B);
  or or_1 (or_1_out, A, B);
  xor xor_2 (xor_2_out, A, B);
  nor nor_1 (nor_1_out, A, B);
  Multiplexer #(.select(3)) multiplexer_1 (
    .in0(and_1_out), .in1(or_1_out), .in2(xor_2_out), .in3(nor_1_out), .in4(out_9), .in5(Less), .out(Result),
    .sel(in_3));  // open: in6, in7, en
endmodule

module _32_Bit_ALU (
  input  Sub,
  input  [2:0] Op,
  input  [31:0] Bus_A,
  input  [31:0] Bus_B,
  output [31:0] out_5,
  output Zero_flag
);

  wire n1_bit_alu_1_c_out, n1_bit_alu_2_c_out, n1_bit_alu_3_c_out, n1_bit_alu_4_c_out, n1_bit_alu_5_c_out,
       n1_bit_alu_6_c_out, n1_bit_alu_7_c_out, n1_bit_alu_8_c_out, n1_bit_alu_9_c_out, n1_bit_alu_10_c_out,
       n1_bit_alu_11_c_out, n1_bit_alu_12_c_out, n1_bit_alu_13_c_out, n1_bit_alu_14_c_out,
       n1_bit_alu_15_c_out, n1_bit_alu_16_c_out, n1_bit_alu_17_c_out, n1_bit_alu_18_c_out,
       n1_bit_alu_19_c_out, n1_bit_alu_20_c_out, n1_bit_alu_21_c_out, n1_bit_alu_22_c_out,
       n1_bit_alu_23_c_out, n1_bit_alu_24_c_out, n1_bit_alu_25_c_out, n1_bit_alu_26_c_out,
       n1_bit_alu_27_c_out, n1_bit_alu_28_c_out, n1_bit_alu_29_c_out, n1_bit_alu_30_c_out,
       n1_bit_alu_31_c_out, n1_bit_alu_32_out_9;

  _1_bit_ALU u_1_bit_alu_1 (
    .in_3(Op), .A(Bus_A[0]), .B(Bus_B[0]), .Less(n1_bit_alu_32_out_9), .Result(out_5[0]), .Sub(Sub),
    .Cin(Sub), .C_out(n1_bit_alu_1_c_out));  // open: out_9
  _1_bit_ALU u_1_bit_alu_2 (
    .in_3(Op), .A(Bus_A[1]), .B(Bus_B[1]), .Less(1'b0), .Result(out_5[1]), .Sub(Sub),
    .Cin(n1_bit_alu_1_c_out), .C_out(n1_bit_alu_2_c_out));  // open: out_9
  _1_bit_ALU u_1_bit_alu_3 (
    .in_3(Op), .A(Bus_A[2]), .B(Bus_B[2]), .Less(1'b0), .Result(out_5[2]), .Sub(Sub),
    .Cin(n1_bit_alu_2_c_out), .C_out(n1_bit_alu_3_c_out));  // open: out_9
  _1_bit_ALU u_1_bit_alu_4 (
    .in_3(Op), .A(Bus_A[3]), .B(Bus_B[3]), .Less(1'b0), .Result(out_5[3]), .Sub(Sub),
    .Cin(n1_bit_alu_3_c_out), .C_out(n1_bit_alu_4_c_out));  // open: out_9
  _1_bit_ALU u_1_bit_alu_5 (
    .in_3(Op), .A(Bus_A[4]), .B(Bus_B[4]), .Less(1'b0), .Result(out_5[4]), .Sub(Sub),
    .Cin(n1_bit_alu_4_c_out), .C_out(n1_bit_alu_5_c_out));  // open: out_9
  _1_bit_ALU u_1_bit_alu_6 (
    .in_3(Op), .A(Bus_A[5]), .B(Bus_B[5]), .Less(1'b0), .Result(out_5[5]), .Sub(Sub),
    .Cin(n1_bit_alu_5_c_out), .C_out(n1_bit_alu_6_c_out));  // open: out_9
  _1_bit_ALU u_1_bit_alu_7 (
    .in_3(Op), .A(Bus_A[6]), .B(Bus_B[6]), .Less(1'b0), .Result(out_5[6]), .Sub(Sub),
    .Cin(n1_bit_alu_6_c_out), .C_out(n1_bit_alu_7_c_out));  // open: out_9
  _1_bit_ALU u_1_bit_alu_8 (
    .in_3(Op), .A(Bus_A[7]), .B(Bus_B[7]), .Less(1'b0), .Result(out_5[7]), .Sub(Sub),
    .Cin(n1_bit_alu_7_c_out), .C_out(n1_bit_alu_8_c_out));  // open: out_9
  _1_bit_ALU u_1_bit_alu_9 (
    .in_3(Op), .A(Bus_A[8]), .B(Bus_B[8]), .Less(1'b0), .Result(out_5[8]), .Sub(Sub),
    .Cin(n1_bit_alu_8_c_out), .C_out(n1_bit_alu_9_c_out));  // open: out_9
  _1_bit_ALU u_1_bit_alu_10 (
    .in_3(Op), .A(Bus_A[9]), .B(Bus_B[9]), .Less(1'b0), .Result(out_5[9]), .Sub(Sub),
    .Cin(n1_bit_alu_9_c_out), .C_out(n1_bit_alu_10_c_out));  // open: out_9
  _1_bit_ALU u_1_bit_alu_11 (
    .in_3(Op), .A(Bus_A[10]), .B(Bus_B[10]), .Less(1'b0), .Result(out_5[10]), .Sub(Sub),
    .Cin(n1_bit_alu_10_c_out), .C_out(n1_bit_alu_11_c_out));  // open: out_9
  _1_bit_ALU u_1_bit_alu_12 (
    .in_3(Op), .A(Bus_A[11]), .B(Bus_B[11]), .Less(1'b0), .Result(out_5[11]), .Sub(Sub),
    .Cin(n1_bit_alu_11_c_out), .C_out(n1_bit_alu_12_c_out));  // open: out_9
  _1_bit_ALU u_1_bit_alu_13 (
    .in_3(Op), .A(Bus_A[12]), .B(Bus_B[12]), .Less(1'b0), .Result(out_5[12]), .Sub(Sub),
    .Cin(n1_bit_alu_12_c_out), .C_out(n1_bit_alu_13_c_out));  // open: out_9
  _1_bit_ALU u_1_bit_alu_14 (
    .in_3(Op), .A(Bus_A[13]), .B(Bus_B[13]), .Less(1'b0), .Result(out_5[13]), .Sub(Sub),
    .Cin(n1_bit_alu_13_c_out), .C_out(n1_bit_alu_14_c_out));  // open: out_9
  _1_bit_ALU u_1_bit_alu_15 (
    .in_3(Op), .A(Bus_A[14]), .B(Bus_B[14]), .Less(1'b0), .Result(out_5[14]), .Sub(Sub),
    .Cin(n1_bit_alu_14_c_out), .C_out(n1_bit_alu_15_c_out));  // open: out_9
  _1_bit_ALU u_1_bit_alu_16 (
    .in_3(Op), .A(Bus_A[15]), .B(Bus_B[15]), .Less(1'b0), .Result(out_5[15]), .Sub(Sub),
    .Cin(n1_bit_alu_15_c_out), .C_out(n1_bit_alu_16_c_out));  // open: out_9
  _1_bit_ALU u_1_bit_alu_17 (
    .in_3(Op), .A(Bus_A[16]), .B(Bus_B[16]), .Less(1'b0), .Result(out_5[16]), .Sub(Sub),
    .Cin(n1_bit_alu_16_c_out), .C_out(n1_bit_alu_17_c_out));  // open: out_9
  _1_bit_ALU u_1_bit_alu_18 (
    .in_3(Op), .A(Bus_A[17]), .B(Bus_B[17]), .Less(1'b0), .Result(out_5[17]), .Sub(Sub),
    .Cin(n1_bit_alu_17_c_out), .C_out(n1_bit_alu_18_c_out));  // open: out_9
  _1_bit_ALU u_1_bit_alu_19 (
    .in_3(Op), .A(Bus_A[18]), .B(Bus_B[18]), .Less(1'b0), .Result(out_5[18]), .Sub(Sub),
    .Cin(n1_bit_alu_18_c_out), .C_out(n1_bit_alu_19_c_out));  // open: out_9
  _1_bit_ALU u_1_bit_alu_20 (
    .in_3(Op), .A(Bus_A[19]), .B(Bus_B[19]), .Less(1'b0), .Result(out_5[19]), .Sub(Sub),
    .Cin(n1_bit_alu_19_c_out), .C_out(n1_bit_alu_20_c_out));  // open: out_9
  _1_bit_ALU u_1_bit_alu_21 (
    .in_3(Op), .A(Bus_A[20]), .B(Bus_B[20]), .Less(1'b0), .Result(out_5[20]), .Sub(Sub),
    .Cin(n1_bit_alu_20_c_out), .C_out(n1_bit_alu_21_c_out));  // open: out_9
  _1_bit_ALU u_1_bit_alu_22 (
    .in_3(Op), .A(Bus_A[21]), .B(Bus_B[21]), .Less(1'b0), .Result(out_5[21]), .Sub(Sub),
    .Cin(n1_bit_alu_21_c_out), .C_out(n1_bit_alu_22_c_out));  // open: out_9
  _1_bit_ALU u_1_bit_alu_23 (
    .in_3(Op), .A(Bus_A[22]), .B(Bus_B[22]), .Less(1'b0), .Result(out_5[22]), .Sub(Sub),
    .Cin(n1_bit_alu_22_c_out), .C_out(n1_bit_alu_23_c_out));  // open: out_9
  _1_bit_ALU u_1_bit_alu_24 (
    .in_3(Op), .A(Bus_A[23]), .B(Bus_B[23]), .Less(1'b0), .Result(out_5[23]), .Sub(Sub),
    .Cin(n1_bit_alu_23_c_out), .C_out(n1_bit_alu_24_c_out));  // open: out_9
  _1_bit_ALU u_1_bit_alu_25 (
    .in_3(Op), .A(Bus_A[24]), .B(Bus_B[24]), .Less(1'b0), .Result(out_5[24]), .Sub(Sub),
    .Cin(n1_bit_alu_24_c_out), .C_out(n1_bit_alu_25_c_out));  // open: out_9
  _1_bit_ALU u_1_bit_alu_26 (
    .in_3(Op), .A(Bus_A[25]), .B(Bus_B[25]), .Less(1'b0), .Result(out_5[25]), .Sub(Sub),
    .Cin(n1_bit_alu_25_c_out), .C_out(n1_bit_alu_26_c_out));  // open: out_9
  _1_bit_ALU u_1_bit_alu_27 (
    .in_3(Op), .A(Bus_A[26]), .B(Bus_B[26]), .Less(1'b0), .Result(out_5[26]), .Sub(Sub),
    .Cin(n1_bit_alu_26_c_out), .C_out(n1_bit_alu_27_c_out));  // open: out_9
  _1_bit_ALU u_1_bit_alu_28 (
    .in_3(Op), .A(Bus_A[27]), .B(Bus_B[27]), .Less(1'b0), .Result(out_5[27]), .Sub(Sub),
    .Cin(n1_bit_alu_27_c_out), .C_out(n1_bit_alu_28_c_out));  // open: out_9
  _1_bit_ALU u_1_bit_alu_29 (
    .in_3(Op), .A(Bus_A[28]), .B(Bus_B[28]), .Less(1'b0), .Result(out_5[28]), .Sub(Sub),
    .Cin(n1_bit_alu_28_c_out), .C_out(n1_bit_alu_29_c_out));  // open: out_9
  _1_bit_ALU u_1_bit_alu_30 (
    .in_3(Op), .A(Bus_A[29]), .B(Bus_B[29]), .Less(1'b0), .Result(out_5[29]), .Sub(Sub),
    .Cin(n1_bit_alu_29_c_out), .C_out(n1_bit_alu_30_c_out));  // open: out_9
  _1_bit_ALU u_1_bit_alu_31 (
    .in_3(Op), .A(Bus_A[30]), .B(Bus_B[30]), .Less(1'b0), .Result(out_5[30]), .Sub(Sub),
    .Cin(n1_bit_alu_30_c_out), .C_out(n1_bit_alu_31_c_out));  // open: out_9
  _1_bit_ALU u_1_bit_alu_32 (
    .in_3(Op), .A(Bus_A[31]), .B(Bus_B[31]), .Less(1'b0), .Result(out_5[31]), .Sub(Sub),
    .Cin(n1_bit_alu_31_c_out), .out_9(n1_bit_alu_32_out_9));  // open: C_out
  nor nor_1 (Zero_flag, out_5[0], out_5[1], out_5[2], out_5[3], out_5[4], out_5[5], out_5[6], out_5[7], out_5[8], out_5[9], out_5[10], out_5[11], out_5[12], out_5[13], out_5[14], out_5[15], out_5[16], out_5[17], out_5[18], out_5[19], out_5[20], out_5[21], out_5[22], out_5[23], out_5[24], out_5[25], out_5[26], out_5[27], out_5[28], out_5[29], out_5[30], out_5[31]);
endmodule

module Register_File (
  input  [4:0] RA,
  input  [4:0] RB,
  input  [31:0] Bus_W,
  input  [4:0] RW,
  input  RegWrite,
  output [31:0] Bus_A,
  output [31:0] Bus_B
);

  wire [11:0] n3x4_zipper_4_wide_1_out_4, n3x4_zipper_4_wide_1_out_5, n3x4_zipper_4_wide_1_out_6,
       n3x4_zipper_4_wide_1_out_7, n3x4_zipper_4_wide_2_out_4, n3x4_zipper_4_wide_2_out_5,
       n3x4_zipper_4_wide_2_out_6, n3x4_zipper_4_wide_2_out_7;
  wire [15:0] decoder_1_out0, decoder_1_out16, decoder_2_out0, decoder_2_out16, decoder_3_out0,
       decoder_3_out16;

  Decoder #(.select(5)) decoder_1 (
    .out0(decoder_1_out0[0]), .out1(decoder_1_out0[1]), .out2(decoder_1_out0[2]), .out3(decoder_1_out0[3]),
    .out4(decoder_1_out0[4]), .out5(decoder_1_out0[5]), .out6(decoder_1_out0[6]), .out7(decoder_1_out0[7]),
    .out8(decoder_1_out0[8]), .out9(decoder_1_out0[9]), .out10(decoder_1_out0[10]),
    .out11(decoder_1_out0[11]), .out12(decoder_1_out0[12]), .out13(decoder_1_out0[13]),
    .out14(decoder_1_out0[14]), .out15(decoder_1_out0[15]), .out16(decoder_1_out16[0]),
    .out17(decoder_1_out16[1]), .out18(decoder_1_out16[2]), .out19(decoder_1_out16[3]),
    .out20(decoder_1_out16[4]), .out21(decoder_1_out16[5]), .out22(decoder_1_out16[6]),
    .out23(decoder_1_out16[7]), .out24(decoder_1_out16[8]), .out25(decoder_1_out16[9]),
    .out26(decoder_1_out16[10]), .out27(decoder_1_out16[11]), .out28(decoder_1_out16[12]),
    .out29(decoder_1_out16[13]), .out30(decoder_1_out16[14]), .out31(decoder_1_out16[15]), .sel(RA));  // open: en
  Decoder #(.select(5)) decoder_2 (
    .out0(decoder_2_out0[0]), .out1(decoder_2_out0[1]), .out2(decoder_2_out0[2]), .out3(decoder_2_out0[3]),
    .out4(decoder_2_out0[4]), .out5(decoder_2_out0[5]), .out6(decoder_2_out0[6]), .out7(decoder_2_out0[7]),
    .out8(decoder_2_out0[8]), .out9(decoder_2_out0[9]), .out10(decoder_2_out0[10]),
    .out11(decoder_2_out0[11]), .out12(decoder_2_out0[12]), .out13(decoder_2_out0[13]),
    .out14(decoder_2_out0[14]), .out15(decoder_2_out0[15]), .out16(decoder_2_out16[0]),
    .out17(decoder_2_out16[1]), .out18(decoder_2_out16[2]), .out19(decoder_2_out16[3]),
    .out20(decoder_2_out16[4]), .out21(decoder_2_out16[5]), .out22(decoder_2_out16[6]),
    .out23(decoder_2_out16[7]), .out24(decoder_2_out16[8]), .out25(decoder_2_out16[9]),
    .out26(decoder_2_out16[10]), .out27(decoder_2_out16[11]), .out28(decoder_2_out16[12]),
    .out29(decoder_2_out16[13]), .out30(decoder_2_out16[14]), .out31(decoder_2_out16[15]), .sel(RB));  // open: en
  Decoder #(.select(5), .disabled(0)) decoder_3 (
    .out0(decoder_3_out0[0]), .out1(decoder_3_out0[1]), .out2(decoder_3_out0[2]), .out3(decoder_3_out0[3]),
    .out4(decoder_3_out0[4]), .out5(decoder_3_out0[5]), .out6(decoder_3_out0[6]), .out7(decoder_3_out0[7]),
    .out8(decoder_3_out0[8]), .out9(decoder_3_out0[9]), .out10(decoder_3_out0[10]),
    .out11(decoder_3_out0[11]), .out12(decoder_3_out0[12]), .out13(decoder_3_out0[13]),
    .out14(decoder_3_out0[14]), .out15(decoder_3_out0[15]), .out16(decoder_3_out16[0]),
    .out17(decoder_3_out16[1]), .out18(decoder_3_out16[2]), .out19(decoder_3_out16[3]),
    .out20(decoder_3_out16[4]), .out21(decoder_3_out16[5]), .out22(decoder_3_out16[6]),
    .out23(decoder_3_out16[7]), .out24(decoder_3_out16[8]), .out25(decoder_3_out16[9]),
    .out26(decoder_3_out16[10]), .out27(decoder_3_out16[11]), .out28(decoder_3_out16[12]),
    .out29(decoder_3_out16[13]), .out30(decoder_3_out16[14]), .out31(decoder_3_out16[15]), .sel(RW),
    .en(RegWrite));
  _3x4_Zipper__4_wide u_3x4_zipper_4_wide_1 (
    .RA(decoder_1_out16), .RB(decoder_2_out16), .RW(decoder_3_out16), .out_4(n3x4_zipper_4_wide_1_out_4),
    .out_5(n3x4_zipper_4_wide_1_out_5), .out_6(n3x4_zipper_4_wide_1_out_6), .out_7(n3x4_zipper_4_wide_1_out_7));
  Register_Cell register_cell_1 (
    .RA(n3x4_zipper_4_wide_1_out_4[3:0]), .RB(n3x4_zipper_4_wide_1_out_4[7:4]),
    .RW(n3x4_zipper_4_wide_1_out_4[11:8]), .BusW(Bus_W), .BusA(Bus_A), .BusB(Bus_B));
  Register_Cell register_cell_2 (
    .RA(n3x4_zipper_4_wide_1_out_5[3:0]), .RB(n3x4_zipper_4_wide_1_out_5[7:4]),
    .RW(n3x4_zipper_4_wide_1_out_5[11:8]), .BusW(Bus_W), .BusA(Bus_A), .BusB(Bus_B));
  Register_Cell register_cell_3 (
    .RA(n3x4_zipper_4_wide_1_out_6[3:0]), .RB(n3x4_zipper_4_wide_1_out_6[7:4]),
    .RW(n3x4_zipper_4_wide_1_out_6[11:8]), .BusW(Bus_W), .BusA(Bus_A), .BusB(Bus_B));
  Register_Cell register_cell_4 (
    .RA(n3x4_zipper_4_wide_1_out_7[3:0]), .RB(n3x4_zipper_4_wide_1_out_7[7:4]),
    .RW(n3x4_zipper_4_wide_1_out_7[11:8]), .BusW(Bus_W), .BusA(Bus_A), .BusB(Bus_B));
  Clock clock_1 ();  // open: out
  _3x4_Zipper__4_wide u_3x4_zipper_4_wide_2 (
    .RA(decoder_1_out0), .RB(decoder_2_out0), .RW(decoder_3_out0), .out_4(n3x4_zipper_4_wide_2_out_4),
    .out_5(n3x4_zipper_4_wide_2_out_5), .out_6(n3x4_zipper_4_wide_2_out_6), .out_7(n3x4_zipper_4_wide_2_out_7));
  Register_Cell_w__0 register_cell_w_0_1 (
    .RA(n3x4_zipper_4_wide_2_out_4[3:0]), .RB(n3x4_zipper_4_wide_2_out_4[7:4]),
    .RW(n3x4_zipper_4_wide_2_out_4[11:8]), .BusW(Bus_W), .BusA(Bus_A), .BusB(Bus_B));
  Register_Cell register_cell_5 (
    .RA(n3x4_zipper_4_wide_2_out_5[3:0]), .RB(n3x4_zipper_4_wide_2_out_5[7:4]),
    .RW(n3x4_zipper_4_wide_2_out_5[11:8]), .BusW(Bus_W), .BusA(Bus_A), .BusB(Bus_B));
  Register_Cell register_cell_6 (
    .RA(n3x4_zipper_4_wide_2_out_6[3:0]), .RB(n3x4_zipper_4_wide_2_out_6[7:4]),
    .RW(n3x4_zipper_4_wide_2_out_6[11:8]), .BusW(Bus_W), .BusA(Bus_A), .BusB(Bus_B));
  Register_Cell register_cell_7 (
    .RA(n3x4_zipper_4_wide_2_out_7[3:0]), .RB(n3x4_zipper_4_wide_2_out_7[7:4]),
    .RW(n3x4_zipper_4_wide_2_out_7[11:8]), .BusW(Bus_W), .BusA(Bus_A), .BusB(Bus_B));

  // Notes on the sheet:
  //   Registers
endmodule

module Register_Cell (
  input  [3:0] RA,
  input  [3:0] RB,
  input  [3:0] RW,
  input  [31:0] BusW,
  output [31:0] BusA,
  output [31:0] BusB
);

  wire [2:0] n3x4_zipper_1_out_4, n3x4_zipper_1_out_5, n3x4_zipper_1_out_6, n3x4_zipper_1_out_7;

  Clock clock_1 ();  // open: out
  _3x4_zipper u_3x4_zipper_1 (
    .RA(RA), .RB(RB), .RW(RW), .out_4(n3x4_zipper_1_out_4), .out_5(n3x4_zipper_1_out_5),
    .out_6(n3x4_zipper_1_out_6), .out_7(n3x4_zipper_1_out_7));
  _32_bit_Register u_32_bit_register_1 (.BusW(BusW), .Control(n3x4_zipper_1_out_4), .BusA(BusA), .BusB(BusB));
  _32_bit_Register u_32_bit_register_2 (.BusW(BusW), .Control(n3x4_zipper_1_out_5), .BusA(BusA), .BusB(BusB));
  _32_bit_Register u_32_bit_register_3 (.BusW(BusW), .Control(n3x4_zipper_1_out_6), .BusA(BusA), .BusB(BusB));
  _32_bit_Register u_32_bit_register_4 (.BusW(BusW), .Control(n3x4_zipper_1_out_7), .BusA(BusA), .BusB(BusB));
endmodule

module Register_Cell_w__0 (
  input  [3:0] RA,
  input  [3:0] RB,
  input  [3:0] RW,
  input  [31:0] BusW,
  output [31:0] BusA,
  output [31:0] BusB
);

  wire [2:0] n3x4_zipper_1_out_4, n3x4_zipper_1_out_5, n3x4_zipper_1_out_6, n3x4_zipper_1_out_7;

  Clock clock_1 ();  // open: out
  _3x4_zipper u_3x4_zipper_1 (
    .RA(RA), .RB(RB), .RW(RW), .out_4(n3x4_zipper_1_out_4), .out_5(n3x4_zipper_1_out_5),
    .out_6(n3x4_zipper_1_out_6), .out_7(n3x4_zipper_1_out_7));
  _32_bit_0_Register _0 (.Control(n3x4_zipper_1_out_4), .BusA(BusA), .BusB(BusB));
  _32_bit_Register _1 (.BusW(BusW), .Control(n3x4_zipper_1_out_5), .BusA(BusA), .BusB(BusB));
  _32_bit_Register _2 (.BusW(BusW), .Control(n3x4_zipper_1_out_6), .BusA(BusA), .BusB(BusB));
  _32_bit_Register _3 (.BusW(BusW), .Control(n3x4_zipper_1_out_7), .BusA(BusA), .BusB(BusB));
endmodule

module _32_bit_Register (
  input  [31:0] BusW,
  input  [2:0] Control,
  output [31:0] BusA,
  output [31:0] BusB
);

  wire clock_1_out;
  wire [31:0] register_1_q;

  Clock clock_1 (.out(clock_1_out));
  Register #(.width(32), .trigger("falling")) register_1 (
    .D(BusW), .en(Control[2]), .Q(register_1_q), .clk(clock_1_out));  // open: clr
  assign BusA = Control[0] ? register_1_q : 32'bz;  // Controlled_Buffer controlled_buffer_1
  assign BusB = Control[1] ? register_1_q : 32'bz;  // Controlled_Buffer controlled_buffer_2

  // Notes on the sheet:
  //   A/B/W
endmodule

module _32_bit_0_Register (
  input  [2:0] Control,
  output [31:0] BusA,
  output [31:0] BusB
);

  Clock clock_1 ();  // open: out
  assign BusA = Control[0] ? {32{1'b0}} : 32'bz;  // Controlled_Buffer controlled_buffer_1
  assign BusB = Control[1] ? {32{1'b0}} : 32'bz;  // Controlled_Buffer controlled_buffer_2
endmodule

module _3x4_zipper (
  input  [3:0] RA,
  input  [3:0] RB,
  input  [3:0] RW,
  output [2:0] out_4,
  output [2:0] out_5,
  output [2:0] out_6,
  output [2:0] out_7
);


  assign out_4 = {RW[0], RB[0], RA[0]};
  assign out_5 = {RW[1], RB[1], RA[1]};
  assign out_6 = {RW[2], RB[2], RA[2]};
  assign out_7 = {RW[3], RB[3], RA[3]};
endmodule

module _3x4_Zipper__4_wide (
  input  [15:0] RA,
  input  [15:0] RB,
  input  [15:0] RW,
  output [11:0] out_4,
  output [11:0] out_5,
  output [11:0] out_6,
  output [11:0] out_7
);


  assign out_4 = {RW[3:0], RB[3:0], RA[3:0]};
  assign out_5 = {RW[7:4], RB[7:4], RA[7:4]};
  assign out_6 = {RW[11:8], RB[11:8], RA[11:8]};
  assign out_7 = {RW[15:12], RB[15:12], RA[15:12]};
endmodule

module Control_Unit (
  input  [5:0] Opcode,
  output Jump,
  output RegDest,
  output BNE,
  output BEQ,
  output MemWrite,
  output MemRead,
  output MemToReg,
  output RegWrite,
  output ALUSrc,
  output ExtOp,
  output R_Type,
  output [3:0] ALUOp
);

  wire ADDI_out, ANDI_out, or_1_out, or_2_out, ORI_out, SLTI_out, XORI_out;

  and u_R_type (R_Type, ~Opcode[5], ~Opcode[4], ~Opcode[3], ~Opcode[2], ~Opcode[1], ~Opcode[0]);  // AND_Gate
  and LW (MemRead, Opcode[5], ~Opcode[4], ~Opcode[3], ~Opcode[2], Opcode[1], Opcode[0]);  // AND_Gate
  and SW (MemWrite, Opcode[5], ~Opcode[4], Opcode[3], ~Opcode[2], Opcode[1], Opcode[0]);  // AND_Gate
  and u_BEQ (BEQ, ~Opcode[5], ~Opcode[4], ~Opcode[3], Opcode[2], ~Opcode[1], ~Opcode[0]);  // AND_Gate
  and ADDI (ADDI_out, ~Opcode[5], ~Opcode[4], Opcode[3], ~Opcode[2], ~Opcode[1], ~Opcode[0]);  // AND_Gate
  or or_1 (or_1_out, MemRead, MemWrite, ADDI_out);
  and SLTI (SLTI_out, ~Opcode[5], ~Opcode[4], Opcode[3], ~Opcode[2], Opcode[1], ~Opcode[0]);  // AND_Gate
  or or_2 (or_2_out, BEQ, BNE);
  and ANDI (ANDI_out, ~Opcode[5], ~Opcode[4], Opcode[3], Opcode[2], ~Opcode[1], ~Opcode[0]);  // AND_Gate
  and ORI (ORI_out, ~Opcode[5], ~Opcode[4], Opcode[3], Opcode[2], ~Opcode[1], Opcode[0]);  // AND_Gate
  and XORI (XORI_out, ~Opcode[5], ~Opcode[4], Opcode[3], Opcode[2], Opcode[1], ~Opcode[0]);  // AND_Gate
  and J (Jump, ~Opcode[5], ~Opcode[4], ~Opcode[3], ~Opcode[2], Opcode[1], ~Opcode[0]);  // AND_Gate
  and u_BNE (BNE, ~Opcode[5], ~Opcode[4], ~Opcode[3], Opcode[2], ~Opcode[1], Opcode[0]);  // AND_Gate
  Priority_Encoder #(.select(4)) priority_encoder_1 (
    .in0(or_1_out), .in2(or_2_out), .in4(ANDI_out), .in5(ORI_out), .in6(XORI_out), .in10(SLTI_out),
    .out(ALUOp));  // open: in1, in3, in7, in8, in9, in11, in12, in13, in14, in15, gs, en_out, en_in
  or u_RegWrite (RegWrite, XORI_out, ORI_out, ANDI_out, SLTI_out, ADDI_out, MemRead, R_Type);
  nor nor_1 (ALUSrc, BNE, BEQ, R_Type);
  nor nor_2 (ExtOp, XORI_out, ORI_out, ANDI_out);

  assign MemToReg = MemRead;
  assign RegDest = R_Type;
endmodule

module PCController (
  input  Zero,
  input  BNE,
  input  BEQ,
  input  Jump,
  output [1:0] PC
);

  wire and_1_out, and_2_out;

  or or_1 (PC[0], and_2_out, and_1_out);
  and and_1 (and_1_out, Zero, BEQ);
  and and_2 (and_2_out, ~Zero, BNE);  // AND_Gate

  assign PC[1] = Jump;
endmodule

module Extender (
  input  [15:0] Imm,
  input  ExtOp,
  output [31:0] Out
);

  wire [31:0] bit_extender_1_out, bit_extender_2_out;

  assign bit_extender_1_out = {{16{1'b0}}, Imm};  // Bit_Extender bit_extender_1
  assign bit_extender_2_out = {{16{Imm[15]}}, Imm};  // Bit_Extender bit_extender_2
  Multiplexer #(.width(32)) multiplexer_1 (
    .in0(bit_extender_1_out), .in1(bit_extender_2_out), .out(Out), .sel(ExtOp));  // open: en
endmodule

module ALUControl (
  input  [3:0] MainCntrl,
  input  [5:0] Funct,
  input  in_3,
  output Sub,
  output [2:0] ALUCntrl
);

  wire ADD_out, priority_encoder_1_p1, priority_encoder_1_p2, priority_encoder_1_p3, priority_encoder_1_p6,
       priority_encoder_1_p7;
  wire [3:0] multiplexer_1_out;

  Multiplexer #(.width(4)) multiplexer_1 (
    .in0(MainCntrl), .in1(Funct[3:0]), .out(multiplexer_1_out), .sel(in_3));  // open: en
  and ADD (ADD_out, ~multiplexer_1_out[3], ~multiplexer_1_out[2], ~multiplexer_1_out[1], ~multiplexer_1_out[0]);  // AND_Gate
  // Priority_Encoder #(.select(4)) priority_encoder_1: pin names not known; wires that end beside it: priority_encoder_1_p1, priority_encoder_1_p2, priority_encoder_1_p3, ADD_out, {Sub, ALUCntrl}, priority_encoder_1_p6, priority_encoder_1_p7
  and u_SUB (priority_encoder_1_p6, ~multiplexer_1_out[3], ~multiplexer_1_out[2], multiplexer_1_out[1], ~multiplexer_1_out[0]);  // AND_Gate
  and OR (priority_encoder_1_p2, ~multiplexer_1_out[3], multiplexer_1_out[2], ~multiplexer_1_out[1], multiplexer_1_out[0]);  // AND_Gate
  and AND (priority_encoder_1_p1, ~multiplexer_1_out[3], multiplexer_1_out[2], ~multiplexer_1_out[1], ~multiplexer_1_out[0]);  // AND_Gate
  and XOR (priority_encoder_1_p3, ~multiplexer_1_out[3], multiplexer_1_out[2], multiplexer_1_out[1], ~multiplexer_1_out[0]);  // AND_Gate
  and SLT (priority_encoder_1_p7, multiplexer_1_out[3], ~multiplexer_1_out[2], multiplexer_1_out[1], ~multiplexer_1_out[0]);  // AND_Gate
endmodule
